# Fritzing sketch Circuit (saved by Fritzing 0.9.5d)
breadboards: 1

parts:
  MCU1 = Raspberry Pi Zero
  GY1 = MPU-6050 Board GY-521 [form="♀ (female)" package=THT]
  Part1 = DHT22 module
  Part2 = DHT22 module
  Part3 = Arduino Uno (Rev3) - ICSP  # not connected
  USBTTL1 = Micro USB B Plug  # not connected
  USBTTL2 = USB A Plug  # not connected

nets:
  GND: MCU1.pin_1, MCU1.pin_6, MCU1.pin_17, MCU1.pin_25, MCU1.pin_34, MCU1.pin_39, GY1.pin2, Part1.GND, Part2.GND
  VCC: MCU1.pin_2, MCU1.pin_4, Part1.VCC, Part2.VCC
  N1: MCU1.pin_3, GY1.pin4
  N2: MCU1.pin_5, GY1.pin3
  N3: MCU1.pin_16, Part1.DATA
  N4: MCU1.pin_18, Part2.DATA

custom parts:
  MPU-6050 Board GY-521: Acelerometro y Giroscopio MPU-6050 Board GY-521
